# Fritzing sketch thereminimum (saved by Fritzing 1.0.4)

parts:
  XIAO_ESP32S1 = XIAO ESP32S3 [package="DIP (Dual Inline) [THT]"]
  Part1 = Adafruit VL53L1X [part_number="Adafruit #3967"]
  SG1 = Buzzer 12mm [part_number=COM-07950 package=buzzer-12mm-ns]

nets:
  N1: XIAO_ESP32S1.D3, Part1.XSHUT
  N2: XIAO_ESP32S1.D4, Part1.GPIO
  N3: XIAO_ESP32S1.D5, SG1.2
  N4: XIAO_ESP32S1.D6, Part1.SDA
  N5: XIAO_ESP32S1.D7, Part1.SCL
  3V3: XIAO_ESP32S1.3V3, Part1.VCC
  GND: XIAO_ESP32S1.GND, Part1.GND, SG1.1

custom parts:
  XIAO ESP32S3: Seeed Studio XIAO ESP32S3 leverages 240MHz Xtensa 32-bit LX7 dual-core processor, supporting both WiFi and BLE 5.0 wireless connectivities, a 2.4GHz Rod antenna, allows for deep sleep mode with power consumption as low as 14μA while supporting lithium battery charging management. Ideal for the Internet of Things, Smart Homes, Wireless wearable devices, Robotics, etc.
  Adafruit VL53L1X: The Adafruit VL53L1X Time of Flight Distance Sensor (also known as VL53L1CX) is a Time of Flight distance sensor that has a massive 4 meter range and LIDAR-like precision. The sensor contains a very tiny invisible laser source and a matching sensor. The VL53L1X can detect the "time of flight", or how long the light has taken to bounce back to the sensor. Since it uses a very narrow light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
  Buzzer 12mm: Buzzer 12mm Spark Fun Electronics SKU : Comp-Buzzer Through hole This is a small 12mm round speaker that operates around the audible 2kHz range. You can use these speakers to create simple music or user interfaces. This is not a true piezoelectric speaker but behaves similarly. Instead of a piezoelectric crystal that vibrates with an electric current, this tiny speaker uses an electromagnet to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
